# Fritzing sketch robolig_receiver (saved by Fritzing 0.9.3b)
breadboards: 1

parts:
  T3_Vakfı1 = Generic shrouded header - 32 pins [package=THT]
  S1 = H-Bridge with L298N
  VCC1 = Battery block 9V
  M1 = DC Motor
  M2 = DC Motor
  J1 = Basic Servo
  U1 = LIPO-2000mAh [package=lipo-2000]  # not connected

nets:
  N1: T3_Vakfı1.pin10, S1.IN4
  N2: T3_Vakfı1.pin11, S1.IN3
  N3: T3_Vakfı1.pin12, S1.IN2
  N4: T3_Vakfı1.pin13, S1.IN1
  5V: T3_Vakfı1.pin15, S1.5V, J1.vcc
  GND: T3_Vakfı1.pin16, S1.GND, VCC1.-, J1.gnd
  N5: T3_Vakfı1.pin22, J1.pulse
  N6: T3_Vakfı1.pin30, S1.ENB
  N7: T3_Vakfı1.pin31, S1.ENA
  N8: S1.12V, VCC1.+
  N9: S1.M1-01, M2.pin_2
  N10: S1.M1-02, M2.pin_1
  N11: S1.M2-01, M1.pin_2
  N12: S1.M2-02, M1.pin_1

notes:
  Li-po Pil Deneyap Kartın Li-po girişine direkt olarak bağlı

custom parts:
  Generic shrouded header - 32 pins: Ülkemizin mühendislik kaynakları kullanılarak geliştirilen Deneyap Kart; güçlü işlemcisi, dayanıklı tasarımı ve çok yönlü giriş/çıkış pinleri ile kullanıcılara Elektronik Programlama, Nesnelerin İnterneti (IoT) ve Yapay Zeka alanlarında başlangıç seviyesinden endüstriyel uygulamalara kadar her seviyede projeyi yapma imkanı sunuyor.
  H-Bridge with L298N: h-bridge
  Battery block 9V: 9 Volt battery block with 200mil pcb footprint spacing
