# Fritzing sketch robolig_sender (saved by Fritzing 0.9.3b)
breadboards: 1

parts:
  Deneyap_Mini1 = Deneyap Mini [package="SIP (Single Inline) [THT]"]
  Parça1 = Thumb Joystick
  Parça2 = Thumb Joystick
  BAT1 = Battery Holders [package=lipo-1100mAh]

nets:
  N1: Deneyap_Mini1.A0, Parça2.HORZ
  N2: Deneyap_Mini1.A1, Parça2.VERT
  N3: Deneyap_Mini1.A2, Parça1.HORZ
  N4: Deneyap_Mini1.A3, Parça1.VERT
  VCC: Deneyap_Mini1.5V, Parça1.VCC, Parça2.VCC, BAT1.+
  GND: Deneyap_Mini1.GND#26, Parça1.GND, Parça2.GND, BAT1.-

notes:
  Sağ Joystick
  Sol Joystick

custom parts:
  Deneyap Mini: Ülkemizin mühendislik kaynakları kullanılarak geliştirilen Deneyap Mini; güçlü işlemcisi, dayanıklı tasarımı ve çok yönlü giriş/çıkış pinleri ile kullanıcılara Elektronik Programlama, Nesnelerin İnterneti (IoT) ve Yapay Zeka alanlarında başlangıç seviyesinden endüstriyel uygulamalara kadar her seviyede projeyi yapma imkanı sunuyor.
